# Fritzing sketch uno (saved by Fritzing 0.9.3b)
breadboards: 1

parts:
  Composant1 = Adafruit 1.44 inch TFT Breakout [part_number="Adafruit #2088"]
  Composant2 = Arduino Uno (Rev3) - ICSP
  Keypad4x1 = Keypad Membran 4x4

nets:
  VIN: Composant1.VIN, Composant2.5V
  GND: Composant1.GND, Composant2.GND
  N1: Composant1.SCK, Composant2.D13/SCK
  N2: Composant1.MOSI, Composant2.D11_PWM/MOSI
  N3: Composant1.TFTCS, Composant2.A0
  N4: Composant1.RESET, Composant2.A1
  N5: Composant1.TFTDC, Composant2.D10_PWM/SS
  N6: Composant2.D8, Keypad4x1.Pin2
  N7: Composant2.D9_PWM, Keypad4x1.Pin1
  N8: Composant2.D2, Keypad4x1.Pin8
  N9: Composant2.D3_PWM, Keypad4x1.Pin7
  N10: Composant2.D4, Keypad4x1.Pin6
  N11: Composant2.D5_PWM, Keypad4x1.Pin5
  N12: Composant2.D6_PWM, Keypad4x1.Pin4
  N13: Composant2.D7, Keypad4x1.Pin3

custom parts:
  Adafruit 1.44 inch TFT Breakout: This lovely little display breakout is the best way to add a small, colorful and bright display to any project. Since the display uses 4-wire SPI to communicate and has its own pixel-addressable frame buffer, it can be used with every kind of microcontroller. Even a very small one with low memory and few pins available! The 1.44" display has 128x128 color pixels. Unlike the low cost "Nokia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
  Keypad Membran 4x4: Membrane Keypad 4x4 Matrix
